// Logisim project computer_16_v0.circ as structural Verilog: 11 circuits, main circuit zzzIncrement
module secondMain (
);

  wire ADD, ADDI, ADDM, ANDD, ANDI, ARITHMITC, AX_HIGH, AX_LOW, AX_WE, BASIC, BOOT, BP_HIGH, BP_LOW, BP_WE,
       BX_HIGH, BX_LOW, BX_WE, C56, C57, C58, C59, C60, C61, C62, C63, CALL, CarryFlag, CF_ADD, CF_ROTATE_L,
       CF_ROTATE_R, CF_SHIFT_L, CF_SHIFT_R, CF_SUB, CLAER, CLC, clock_1_out, clock_2_out, clock_3_out,
       clock_4_out, clock_5_out, clock_6_out, clock_7_out, clock_8_out, clock_9_out, clock_10_out,
       clock_11_out, clock_12_out, clock_13_out, clock_14_out, CMP, CMPI, COMPRISON, CX_HIGH, CX_LOW, CX_WE,
       DEC, DI_HIGH, DI_LOW, DI_WE, DIV, DIVI, DX_HIGH, DX_LOW, DX_WE, F_HIGH, F_LOW, F_WE, FLOW, HALT, INC,
       INN, JA, JAE, JBE, JC, JE, JL, JMP, JNC, JNS, JNZ, JS, LAD, LOAD, LOGIC, LOGIC_4bit, LOOPP, MOV, MOVI,
       MUL, MULI, not_1_out, NOTT, OF_ADD, OF_SUB, or_20_out, ORI, ORR, OUTT, POP, PUSH, RET, ROLI, ROLL,
       RORI, RORR, SHL, SHLI, SHR, SHRI, SI_HIGH, SI_LOW, SI_WE, SP_HIGH, SP_LOW, SP_WE, STC, STOR, STR, SUB,
       SUBI, SUBM, TEST, XCHG, XORI, XORR, zzzreasetip_1_reseat;
  wire [2:0] Counter, multiplexer_13_out, zzzincrement_3b_1_outcounter;
  wire [3:0] F_inALU;
  wire [7:0] multiplexer_14_out;
  wire [15:0] ADD_High, AddressBus, AND_High, AX_inData, AX_inHigh, AX_inLow, AX_outData, BOOT_data,
       BP_inData, BP_inHigh, BP_inLow, BP_outData, BX_inData, BX_inHigh, BX_inLow, BX_outData, CX_inData,
       CX_inHigh, CX_inLow, CX_outData, DataBus, DEC_High, demultiplexer_1_out1, DI_inData, DI_inHigh,
       DI_inLow, DI_outData, DIV_High, DIV_Low, DX_inData, DX_inHigh, DX_inLow, DX_outData, F_inData,
       F_inHigh, F_inLow, F_outData, inDataALU1, inDataALU2, inDataLow, IP_q, IR, MAR_q, MUL_High, MUL_Low,
       multiplexer_5_out, multiplexer_6_out, multiplexer_7_out, multiplexer_8_out, multiplexer_12_out,
       NOT_High, or_10_out, OR_High, outDataALU_1, outDataALU_2, RAAM_dout, ROTATE_L_High, ROTATE_R_High,
       SHIFT_L_High, SHIFT_R_High, SI_inData, SI_inHigh, SI_inLow, SI_outData, SP_inData, SP_inHigh,
       SP_inLow, SP_outData, XOR_High, zzzincrement_1_outaddressinstrucre;
  wire [63:0] ControlBus, RoomSet;

  ROM #(.addrWidth(16), .dataWidth(16)) u_BOOT (.addr(AddressBus), .data(BOOT_data));
  RAM #(.addrWidth(16), .dataWidth(16), .enables("line")) RAAM (
    .addr(AddressBus), .we(ControlBus[1]), .clk(clock_1_out), .din(DataBus), .dout(RAAM_dout));
  Clock clock_1 (.out(clock_1_out));
  Demultiplexer #(.disabled("Z"), .enable("true"), .tristate("true"), .width(16)) demultiplexer_1 (
    .out0(DataBus), .out1(demultiplexer_1_out1), .in(RAAM_dout), .sel(ControlBus[3]), .en(ControlBus[2]));
  Demultiplexer #(.disabled("Z"), .tristate("true"), .width(16)) demultiplexer_2 (
    .out0(outDataALU_1), .out1(outDataALU_2), .in(demultiplexer_1_out1), .sel(ControlBus[4]));
  assign DataBus = ControlBus[0] ? BOOT_data : 16'bz;  // Controlled_Buffer controlled_buffer_1
  Decoder #(.select(4)) decoder_1 (
    .out0(AX_HIGH), .out1(BX_HIGH), .out2(CX_HIGH), .out3(DX_HIGH), .out4(BP_HIGH), .out5(DI_HIGH),
    .out6(SI_HIGH), .out7(SP_HIGH), .out15(F_HIGH), .sel(ControlBus[59:56]), .en(ControlBus[14]));  // open: out8, out9, out10, out11, out12, out13, out14
  Decoder #(.select(4), .tristate("true")) decoder_2 (
    .out0(AX_LOW), .out1(BX_LOW), .out2(CX_LOW), .out3(DX_LOW), .out4(BP_LOW), .out5(DI_LOW), .out6(SI_LOW),
    .out7(SP_LOW), .out15(F_LOW), .sel(ControlBus[63:60]), .en(ControlBus[19]));  // open: out8, out9, out10, out11, out12, out13, out14
  Multiplexer #(.width(16)) multiplexer_1 (.in0(16'h1), .in1(outDataALU_1), .out(inDataALU1), .sel(ControlBus[25]));
  Multiplexer #(.width(16)) multiplexer_2 (.in0(16'h1), .in1(outDataALU_2), .out(inDataALU2), .sel(ControlBus[26]));
  or or_1 (AX_WE, AX_HIGH, AX_LOW);
  or or_2 (BX_WE, BX_HIGH, BX_LOW);
  or or_3 (CX_WE, CX_HIGH, CX_LOW);
  or or_4 (DX_WE, DX_HIGH, DX_LOW);
  or or_5 (BP_WE, BP_HIGH, BP_LOW);
  or or_6 (DI_WE, DI_HIGH, DI_LOW);
  or or_7 (SI_WE, SI_HIGH, SI_LOW);
  or or_8 (SP_WE, SP_HIGH, SP_LOW);
  or or_9 (F_WE, F_HIGH, ControlBus[12], F_LOW);
  Multiplexer #(.disabled("Z"), .enable("true"), .select(4), .width(16)) multiplexer_3 (
    .in0(ADD_High), .in1(DEC_High), .in2(MUL_High), .in3(DIV_High), .in4(ADD_High), .in5(DEC_High),
    .in6(AND_High), .in7(OR_High), .in8(XOR_High), .in9(NOT_High), .in10(SHIFT_L_High), .in11(SHIFT_R_High),
    .in12(ROTATE_L_High), .in13(ROTATE_R_High), .in14({16{1'b0}}), .in15({16{1'b0}}), .out(DataBus),
    .sel(ControlBus[35:32]), .en(ControlBus[23]));
  Multiplexer #(.disabled("Z"), .enable("true"), .select(4), .width(16)) multiplexer_4 (
    .in0({16{1'b0}}), .in1({16{1'b0}}), .in2(MUL_Low), .in3(DIV_Low), .in4({16{1'b0}}), .in5({16{1'b0}}),
    .in6({16{1'b0}}), .in7({16{1'b0}}), .in8({16{1'b0}}), .in9({16{1'b0}}), .in10({16{1'b0}}),
    .in11({16{1'b0}}), .in12({16{1'b0}}), .in13({16{1'b0}}), .in14({16{1'b0}}), .in15({16{1'b0}}),
    .out(inDataLow), .sel(ControlBus[35:32]), .en(ControlBus[24]));
  Demultiplexer #(.select(2), .tristate("true"), .width(16)) demultiplexer_3 (
    .out0(DataBus), .out1(inDataLow), .out2(outDataALU_1), .out3(outDataALU_2), .in(multiplexer_5_out),
    .sel(ControlBus[17:16]));
  Multiplexer #(.disabled("Z"), .enable("true"), .select(4), .width(16)) multiplexer_5 (
    .in0(AX_outData), .in1(BX_outData), .in2(CX_outData), .in3(DX_outData), .in4(BP_outData),
    .in5(DI_outData), .in6(SI_outData), .in7(SP_outData), .in15(F_outData), .out(multiplexer_5_out),
    .sel(ControlBus[59:56]), .en(ControlBus[15]));  // open: in8, in9, in10, in11, in12, in13, in14
  Demultiplexer #(.select(2), .tristate("true"), .width(16)) demultiplexer_4 (
    .out0(DataBus), .out1(inDataLow), .out2(outDataALU_1), .out3(outDataALU_2), .in(multiplexer_6_out),
    .sel(ControlBus[22:21]));
  Multiplexer #(.disabled("Z"), .enable("true"), .select(4), .width(16)) multiplexer_6 (
    .in0(AX_outData), .in1(BX_outData), .in2(CX_outData), .in3(DX_outData), .in4(BP_outData),
    .in5(DI_outData), .in6(SI_outData), .in7(SP_outData), .in15(F_outData), .out(multiplexer_6_out),
    .sel(ControlBus[63:60]), .en(ControlBus[20]));  // open: in8, in9, in10, in11, in12, in13, in14
  Multiplexer #(.disabled("Z"), .width(16)) multiplexer_7 (
    .in0(DataBus), .in1(inDataLow), .out(multiplexer_7_out), .sel(ControlBus[13]));
  Multiplexer #(.disabled("Z"), .width(16)) multiplexer_8 (
    .in0(DataBus), .in1(inDataLow), .out(multiplexer_8_out), .sel(ControlBus[18]));
  Demultiplexer #(.enable("true"), .select(4), .width(16)) demultiplexer_5 (
    .out0(AX_inHigh), .out1(BX_inHigh), .out2(CX_inHigh), .out3(DX_inHigh), .out4(BP_inHigh),
    .out5(DI_inHigh), .out6(SI_inHigh), .out7(SP_inHigh), .out15(F_inHigh), .in(multiplexer_7_out),
    .sel(ControlBus[59:56]), .en(ControlBus[14]));  // open: out8, out9, out10, out11, out12, out13, out14
  Demultiplexer #(.enable("true"), .select(4), .width(16)) demultiplexer_6 (
    .out0(AX_inLow), .out1(BX_inLow), .out2(CX_inLow), .out3(DX_inLow), .out4(BP_inLow), .out5(DI_inLow),
    .out6(SI_inLow), .out7(SP_inLow), .out15(F_inLow), .in(multiplexer_8_out), .sel(ControlBus[63:60]),
    .en(ControlBus[19]));  // open: out8, out9, out10, out11, out12, out13, out14
  Comparator #(.mode("unsigned"), .width(16)) comparator_1 (
    .a(DataBus), .b({16{1'b0}}), .eq(F_inALU[0]));  // open: gt, lt
  Comparator #(.mode("unsigned"), .width(1)) comparator_2 (.a(DataBus[15]), .b(1'b1), .eq(F_inALU[1]));  // open: gt, lt
  assign or_10_out = F_inHigh | F_inLow;  // OR_Gate or_10, 16 bits wide
  Multiplexer #(.select(4)) multiplexer_9 (
    .in0(CF_ADD), .in1(CF_SUB), .in2(1'b0), .in3(1'b0), .in4(CF_ADD), .in5(CF_SUB), .in6(1'b0), .in7(1'b0),
    .in8(CF_SHIFT_L), .in9(CF_SHIFT_R), .in10(CF_ROTATE_L), .in11(CF_ROTATE_R), .in12(1'b0), .in13(1'b0),
    .in14(1'b0), .in15(1'b0), .out(CarryFlag), .sel(ControlBus[35:32]));
  assign AX_inData = AX_inHigh | AX_inLow;  // OR_Gate or_11, 16 bits wide
  assign BX_inData = BX_inHigh | BX_inLow;  // OR_Gate or_12, 16 bits wide
  assign CX_inData = CX_inHigh | CX_inLow;  // OR_Gate or_13, 16 bits wide
  assign DX_inData = DX_inHigh | DX_inLow;  // OR_Gate or_14, 16 bits wide
  assign BP_inData = BP_inHigh | BP_inLow;  // OR_Gate or_15, 16 bits wide
  assign DI_inData = DI_inHigh | DI_inLow;  // OR_Gate or_16, 16 bits wide
  assign SI_inData = SI_inHigh | SI_inLow;  // OR_Gate or_17, 16 bits wide
  assign SP_inData = SP_inHigh | SP_inLow;  // OR_Gate or_18, 16 bits wide
  Multiplexer #(.select(2), .width(16)) multiplexer_10 (
    .in0(or_10_out), .in1({{12{1'b0}}, F_inALU[3], CarryFlag, F_inALU[1:0]}), .out(F_inData),
    .sel({1'b0, ControlBus[12]}));  // open: in2, in3
  zADD16 zadd16_1 (
    .inALU1(inDataALU1), .inALU2(inDataALU2), .ADD_High(ADD_High), .CF(CF_ADD), .OVF(OF_ADD));  // open: iCF
  zSUB16 zsub16_1 (
    .inALU1(inDataALU1), .inALU2(inDataALU2), .SUB_High(DEC_High), .CF(CF_SUB), .OVF(OF_SUB));  // open: iCF
  Multiplier #(.width(16)) multiplier_1 (.a(inDataALU1), .b(inDataALU2), .out(MUL_High), .cout(MUL_Low));  // open: cin
  Divider #(.width(16)) divider_1 (.a(inDataALU1), .b(inDataALU2), .out(DIV_High), .rem(DIV_Low));  // open: upper
  Register #(.width(16)) AX (.D(AX_inData), .en(AX_WE), .clk(clock_2_out), .Q(AX_outData));  // open: clr
  Clock clock_2 (.out(clock_2_out));
  Register #(.width(16)) BX (.D(BX_inData), .en(BX_WE), .clk(clock_3_out), .Q(BX_outData));  // open: clr
  Clock clock_3 (.out(clock_3_out));
  Register #(.width(16)) CX (.D(CX_inData), .en(CX_WE), .clk(clock_4_out), .Q(CX_outData));  // open: clr
  Clock clock_4 (.out(clock_4_out));
  Register #(.width(16)) DX (.D(DX_inData), .en(DX_WE), .clk(clock_5_out), .Q(DX_outData));  // open: clr
  Clock clock_5 (.out(clock_5_out));
  Register #(.width(16)) BP (.D(BP_inData), .en(BP_WE), .clk(clock_6_out), .Q(BP_outData));  // open: clr
  Clock clock_6 (.out(clock_6_out));
  Register #(.width(16)) DI (.D(DI_inData), .en(DI_WE), .clk(clock_7_out), .Q(DI_outData));  // open: clr
  Clock clock_7 (.out(clock_7_out));
  Register #(.width(16)) SI (.D(SI_inData), .en(SI_WE), .clk(clock_8_out), .Q(SI_outData));  // open: clr
  Clock clock_8 (.out(clock_8_out));
  Register #(.width(16)) SP (.D(SP_inData), .en(SP_WE), .clk(clock_9_out), .Q(SP_outData));  // open: clr
  Clock clock_9 (.out(clock_9_out));
  Multiplexer #(.select(4)) multiplexer_11 (
    .in0(OF_ADD), .in1(OF_SUB), .in2(1'b0), .in3(1'b0), .in4(OF_ADD), .in5(OF_SUB), .in6(1'b0), .in7(1'b0),
    .in8(1'b0), .in9(1'b0), .in10(1'b0), .in11(1'b0), .in12(1'b0), .in13(1'b0), .in14(1'b0), .in15(1'b0),
    .out(F_inALU[3]), .sel(ControlBus[35:32]));
  zzzIncrement zzzincrement_1 (.inAddressInstrucre(IP_q), .outAddressInstrucre(zzzincrement_1_outaddressinstrucre));
  Multiplexer #(.width(16)) multiplexer_12 (
    .in0(zzzincrement_1_outaddressinstrucre), .in1(DataBus), .out(multiplexer_12_out), .sel(not_1_out));
  not not_1 (not_1_out, ControlBus[9]);
  Clock clock_10 (.out(clock_10_out));
  Clock clock_11 (.out(clock_11_out));
  assign AND_High = inDataALU1 & inDataALU2;  // AND_Gate and_1, 16 bits wide
  assign OR_High = inDataALU1 | inDataALU2;  // OR_Gate or_19, 16 bits wide
  assign XOR_High = inDataALU1 ^ inDataALU2;  // XOR_Gate xor_1, 16 bits wide
  assign NOT_High = ~inDataALU1;  // NOT_Gate not_2, 16 bits wide
  Register #(.width(16)) IP (
    .D(multiplexer_12_out), .en(ControlBus[8]), .clk(clock_10_out), .Q(IP_q), .clr(ControlBus[7]));
  Register #(.width(16)) MAR (.D(DataBus), .en(ControlBus[10]), .clk(clock_12_out), .Q(MAR_q));  // open: clr
  Clock clock_12 (.out(clock_12_out));
  Register #(.width(16)) FLAGS (.D(F_inData), .en(F_WE), .clk(clock_11_out), .Q(F_outData));  // open: clr
  zSHIFT_L zshift_l_1 (.inALU1(inDataALU1), .inALU2(inDataALU2), .CF(CF_SHIFT_L), .result(SHIFT_L_High));
  zSHIFT_R zshift_r_1 (.inALU1(inDataALU1), .inALU2(inDataALU2), .CF(CF_SHIFT_R), .result(SHIFT_R_High));
  zROTATE_L zrotate_l_1 (.inALU1(inDataALU1), .inALU2(inDataALU2), .CF(CF_ROTATE_L), .result(ROTATE_L_High));
  zROTATE_R zrotate_r_1 (.inALU1(inDataALU1), .inALU2(inDataALU2), .CF(CF_ROTATE_R), .result(ROTATE_R_High));
  assign AddressBus = ControlBus[9] ? IP_q : 16'bz;  // Controlled_Buffer controlled_buffer_2
  assign AddressBus = ControlBus[11] ? MAR_q : 16'bz;  // Controlled_Buffer controlled_buffer_3
  Clock clock_13 (.out(clock_13_out));
  zzzIncrement_3b zzzincrement_3b_1 (.inCounter(Counter), .outCounter(zzzincrement_3b_1_outcounter));
  Decoder #(.enable("false"), .select(6)) decoder_3 (
    .out0(BOOT), .out1(LOAD), .out2(STOR), .out3(LAD), .out4(STR), .out5(MOV), .out6(MOVI), .out7(PUSH),
    .out8(POP), .out9(XCHG), .out10(INN), .out11(OUTT), .out12(ADD), .out13(ADDI), .out14(ADDM), .out15(SUB),
    .out16(SUBI), .out17(SUBM), .out18(MUL), .out19(MULI), .out20(DIV), .out21(DIVI), .out22(INC),
    .out23(DEC), .out24(ANDD), .out25(ANDI), .out26(ORR), .out27(ORI), .out28(XORR), .out29(XORI),
    .out30(NOTT), .out31(SHL), .out32(SHLI), .out33(SHR), .out34(SHRI), .out35(ROLL), .out36(ROLI),
    .out37(RORR), .out38(RORI), .out39(CMP), .out40(CMPI), .out41(TEST), .out42(JMP), .out43(JE),
    .out44(JNZ), .out45(JC), .out46(JNC), .out47(JS), .out48(JNS), .out49(JA), .out50(JL), .out51(JAE),
    .out52(JBE), .out53(CALL), .out54(RET), .out55(LOOPP), .out56(CLC), .out57(STC), .out58(HALT),
    .sel(IR[5:0]));  // open: out59, out60, out61, out62, out63
  Register #(.width(16)) u_IR (.D(DataBus), .en(ControlBus[5]), .clk(clock_13_out), .Q(IR));  // open: clr
  Register #(.width(3)) u_Counter (.D(multiplexer_13_out), .clk(clock_14_out), .Q(Counter));  // open: en, clr
  Multiplexer #(.width(3)) multiplexer_13 (
    .in0(zzzincrement_3b_1_outcounter), .in1(3'b000), .out(multiplexer_13_out), .sel(zzzreasetip_1_reseat));
  Clock clock_14 (.out(clock_14_out));
  zzzReasetIP zzzreasetip_1 (.inDataBus(DataBus), .C61Reseat(ControlBus[6]), .Reseat(zzzreasetip_1_reseat));
  ROM #(.addrWidth(9), .dataWidth(64)) Opcode (.addr({IR[5:0], Counter}), .data(RoomSet));
  Comparator #(.mode("unsigned"), .width(9)) comparator_3 (
    .a({9{1'b0}}), .b({XCHG, POP, PUSH, MOVI, MOV, STR, LAD, STOR, LOAD}), .lt(BASIC));  // open: gt, eq
  Comparator #(.mode("unsigned"), .width(12)) comparator_4 (
    .a({12{1'b0}}), .b({DEC, INC, DIVI, DIV, MULI, MUL, SUBM, SUBI, SUB, ADDM, ADDI, ADD}), .lt(ARITHMITC));  // open: gt, eq
  Comparator #(.mode("unsigned"), .width(3)) comparator_5 (
    .a(3'b000), .b({HALT, STC, CLC}), .lt(CLAER));  // open: gt, eq
  Comparator #(.mode("unsigned"), .width(4)) comparator_6 (
    .a(4'b0000), .b({RORI, ROLI, SHRI, SHLI}), .lt(LOGIC_4bit));  // open: gt, eq
  assign {C63, C62, C61, C60, C59, C58, C57, C56} = IR[13:6] & multiplexer_14_out;  // AND_Gate and_2, 8 bits wide
  Multiplexer #(.width(8)) multiplexer_14 (.in0({8{1'b0}}), .in1({8{1'b1}}), .out(multiplexer_14_out), .sel(or_20_out));
  or or_20 (or_20_out, BASIC, ARITHMITC, LOGIC, COMPRISON);
  Comparator #(.mode("unsigned"), .width(14)) comparator_7 (
    .a({14{1'b0}}), .b({LOOPP, RET, CALL, JBE, JAE, JL, JA, JNS, JS, JNC, JC, JNZ, JE, JMP}), .lt(FLOW));  // open: gt, eq
  Comparator #(.mode("unsigned"), .width(12)) comparator_8 (
    .a({12{1'b0}}), .b({LOGIC_4bit, RORR, ROLL, SHR, SHL, NOTT, XORI, XORR, ORI, ORR, ANDI, ANDD}), .lt(LOGIC));  // open: gt, eq
  Comparator #(.mode("unsigned"), .width(3)) comparator_9 (
    .a(3'b000), .b({TEST, CMPI, CMP}), .lt(COMPRISON));  // open: gt, eq
  assign outDataALU_2 = LOGIC_4bit ? {{12{1'b0}}, IR[13:10]} : 16'bz;  // Controlled_Buffer controlled_buffer_4
  or or_21 (ControlBus[0], RoomSet[0], 1'b0);
  or or_22 (ControlBus[1], RoomSet[1], 1'b0);
  or or_23 (ControlBus[2], RoomSet[2], 1'b0);
  or or_24 (ControlBus[3], RoomSet[3], 1'b0);
  or or_25 (ControlBus[4], RoomSet[4], 1'b0);
  or or_26 (ControlBus[5], RoomSet[5], 1'b0);
  or or_27 (ControlBus[6], RoomSet[6], 1'b0);
  or or_28 (ControlBus[7], RoomSet[7], 1'b0);
  or or_29 (ControlBus[8], RoomSet[8], 1'b0);
  or or_30 (ControlBus[9], RoomSet[9], 1'b0);
  or or_31 (ControlBus[10], RoomSet[10], 1'b0);
  or or_32 (ControlBus[11], RoomSet[11], 1'b0);
  or or_33 (ControlBus[12], RoomSet[12], 1'b0);
  or or_34 (ControlBus[13], RoomSet[13], 1'b0);
  or or_35 (ControlBus[14], RoomSet[14], 1'b0);
  or or_36 (ControlBus[15], RoomSet[15], 1'b0);
  or or_37 (ControlBus[16], RoomSet[16], 1'b0);
  or or_38 (ControlBus[17], RoomSet[17], 1'b0);
  or or_39 (ControlBus[18], RoomSet[18], 1'b0);
  or or_40 (ControlBus[19], RoomSet[19], 1'b0);
  or or_41 (ControlBus[20], RoomSet[20], 1'b0);
  or or_42 (ControlBus[21], RoomSet[21], 1'b0);
  or or_43 (ControlBus[22], RoomSet[22], 1'b0);
  or or_44 (ControlBus[23], RoomSet[23], 1'b0);
  or or_45 (ControlBus[24], RoomSet[24], 1'b0);
  or or_46 (ControlBus[25], RoomSet[25], 1'b0);
  or or_47 (ControlBus[26], RoomSet[26], 1'b0);
  or or_48 (ControlBus[27], RoomSet[27], 1'b0);
  or or_49 (ControlBus[28], RoomSet[28], 1'b0);
  or or_50 (ControlBus[29], RoomSet[29], 1'b0);
  or or_51 (ControlBus[30], RoomSet[30], 1'b0);
  or or_52 (ControlBus[31], RoomSet[31], 1'b0);
  or or_53 (ControlBus[32], RoomSet[32], 1'b0);
  or or_54 (ControlBus[33], RoomSet[33], 1'b0);
  or or_55 (ControlBus[34], RoomSet[34], 1'b0);
  or or_56 (ControlBus[35], RoomSet[35], 1'b0);
  or or_57 (ControlBus[36], RoomSet[36], 1'b0);
  or or_58 (ControlBus[37], RoomSet[37], 1'b0);
  or or_59 (ControlBus[38], RoomSet[38], 1'b0);
  or or_60 (ControlBus[39], RoomSet[39], 1'b0);
  or or_61 (ControlBus[40], RoomSet[40], 1'b0);
  or or_62 (ControlBus[41], RoomSet[41], 1'b0);
  or or_63 (ControlBus[42], RoomSet[42], 1'b0);
  or or_64 (ControlBus[43], RoomSet[43], 1'b0);
  or or_65 (ControlBus[44], RoomSet[44], 1'b0);
  or or_66 (ControlBus[45], RoomSet[45], 1'b0);
  or or_67 (ControlBus[46], RoomSet[46], 1'b0);
  or or_68 (ControlBus[47], RoomSet[47], 1'b0);
  or or_69 (ControlBus[48], RoomSet[48], 1'b0);
  or or_70 (ControlBus[49], RoomSet[49], 1'b0);
  or or_71 (ControlBus[50], RoomSet[50], 1'b0);
  or or_72 (ControlBus[51], RoomSet[51], 1'b0);
  or or_73 (ControlBus[52], RoomSet[52], 1'b0);
  or or_74 (ControlBus[53], RoomSet[53], 1'b0);
  or or_75 (ControlBus[54], RoomSet[54], 1'b0);
  or or_76 (ControlBus[55], RoomSet[55], 1'b0);
  or or_77 (ControlBus[56], RoomSet[56], C56);
  or or_78 (ControlBus[57], RoomSet[57], C57);
  or or_79 (ControlBus[58], RoomSet[58], C58);
  or or_80 (ControlBus[59], RoomSet[59], C59);
  or or_81 (ControlBus[60], RoomSet[60], C60);
  or or_82 (ControlBus[61], RoomSet[61], C61);
  or or_83 (ControlBus[62], RoomSet[62], C62);
  or or_84 (ControlBus[63], RoomSet[63], C63);

  // Other names for the same wires on the sheet: JZ = JE; JNE = JNC; JG = JA; REF = JL; ZeroFlag = F_inALU[0];
  //   SignFlag = F_inALU[1]; F_inALU[2] = CarryFlag; OverFlowFlag = F_inALU[3]; INC_High[15:0] = ADD_High;
  //   SUB_High[15:0] = DEC_High

  // Notes on the sheet:
  //   contents of BOOT (hex, n*v repeats v):
  //   1 7 41 9 402 8 39 ff 1f 20 a ffff
  //   0
  //   0
  //   0
  //   0
  //   0
  //   0
  //   0
  //   0
  //   0
  //   0
  //   0
  //   0
  //   OF
  //   CF
  //   SF
  //   ZF
  //   contents of Opcode (hex, n*v repeats v):
  //   343 80 364 4*0 ffffffffffffffff 704 4804 364 4*0 ffffffffffffffff 704 100802 364 4*0
  //   ffffffffffffffff 6938c 2404 1b4 4*0 ffffffffffffffff c38c 20402 1b4 4*0 ffffffffffffffff 22000 1b4
  //   5*0 ffffffffffffffff 2184 1b4 5*0 ffffffffffffffff 20200 6*0 ffffffffffffffff 7*0 ffffffffffffffff
endmodule

module zzzIncrement (
  input  [15:0] inAddressInstrucre,
  output [15:0] outAddressInstrucre
);

  Adder #(.width(16)) adder_1 (.a(inAddressInstrucre), .b(16'h1), .out(outAddressInstrucre));  // open: cin, cout
endmodule

module zzzIncrement_3b (
  input  [2:0] inCounter,
  output [2:0] outCounter
);

  Adder #(.width(3)) adder_1 (.a(inCounter), .b(3'b001), .out(outCounter));  // open: cin, cout
endmodule

module zzzReasetIP (
  input  [15:0] inDataBus,
  input  C61Reseat,
  output Reseat
);

  wire and_1_out, clock_1_out, clock_2_out, comparator_1_eq, register_1_q, register_2_q;

  Comparator #(.mode("unsigned"), .width(16)) comparator_1 (
    .a(inDataBus), .b({16{1'b1}}), .eq(comparator_1_eq));  // open: gt, lt
  Register #(.width(1)) register_1 (.D(1'b1), .en(comparator_1_eq), .clk(clock_1_out), .Q(register_1_q));  // open: clr
  Clock clock_1 (.out(clock_1_out));
  Register #(.width(1)) register_2 (.D(register_1_q), .clk(clock_2_out), .Q(register_2_q));  // open: en, clr
  Clock clock_2 (.out(clock_2_out));
  and and_1 (and_1_out, comparator_1_eq, ~register_2_q);  // AND_Gate
  and and_2 (Reseat, ~and_1_out, C61Reseat);  // AND_Gate
endmodule

module zADD16 (
  input  [15:0] inALU1,
  input  [15:0] inALU2,
  input  iCF,
  output [15:0] ADD_High,
  output CF,
  output OVF
);

  wire xnor_1_out, xor_1_out;

  xnor xnor_1 (xnor_1_out, inALU2[15], inALU1[15]);
  xor xor_1 (xor_1_out, inALU1[15], ADD_High[15]);
  Adder #(.width(16)) adder_1 (.a(inALU1), .b(inALU2), .out(ADD_High), .cin(iCF), .cout(CF));
  and and_1 (OVF, xnor_1_out, xor_1_out);
endmodule

module zSUB16 (
  input  [15:0] inALU1,
  input  [15:0] inALU2,
  input  iCF,
  output [15:0] SUB_High,
  output CF,
  output OVF
);

  wire xor_1_out, xor_2_out;

  xor xor_1 (xor_1_out, inALU2[15], inALU2[15]);
  and and_1 (OVF, xor_1_out, xor_2_out);
  Subtractor #(.width(16)) subtractor_1 (.a(inALU1), .b(inALU2), .out(SUB_High), .bin(iCF), .bout(CF));
  xor xor_2 (xor_2_out, inALU2[15], SUB_High[15]);
endmodule

module zSHIFT_L (
  input  [15:0] inALU1,
  input  [15:0] inALU2,
  output CF,
  output [15:0] result
);

  Shifter #(.width(17)) shifter_1 (.in({1'b0, inALU1}), .\dist ({1'b0, inALU2[3:0]}), .out({CF, result}));
endmodule

module zSHIFT_R (
  input  [15:0] inALU1,
  input  [15:0] inALU2,
  output CF,
  output [15:0] result
);

  Shifter #(.shift("lr"), .width(17)) shifter_1 (.in({inALU1, 1'b0}), .\dist ({1'b0, inALU2[3:0]}), .out({result, CF}));
endmodule

module zROTATE_L (
  input  [15:0] inALU1,
  input  [15:0] inALU2,
  output CF,
  output [15:0] result
);

  Shifter #(.shift("rl"), .width(16)) shifter_1 (.in(inALU1), .\dist (inALU2[3:0]), .out({result[15:1], CF}));

  assign result[0] = CF;
endmodule

module zROTATE_R (
  input  [15:0] inALU1,
  input  [15:0] inALU2,
  output CF,
  output [15:0] result
);

  Shifter #(.shift("rr"), .width(16)) shifter_1 (.in(inALU1), .\dist (inALU2[3:0]), .out({CF, result[14:0]}));

  assign result[15] = CF;
endmodule

module test (
  input  [3:0] Data,
  input  B0,
  input  B1,
  input  B2,
  input  B3,
  input  S1,
  input  S0,
  output out_8
);

  wire and_1_out, and_2_out, and_3_out, and_4_out, and_5_out, and_6_out, and_7_out, and_8_out, clock_1_out,
       clock_2_out, clock_3_out, not_1_out, not_2_out;
  wire [3:0] adder_1_out, adder_2_out, AX_q, BX_q, Counter_q, IR_q, MAR_q, multiplexer_1_out, rom_1_data;

  Register #(.width(4)) IR (.Q(IR_q));  // open: D, en, clk, clr
  Register #(.width(4)) Counter (.D(adder_1_out), .clk(clock_1_out), .Q(Counter_q));  // open: en, clr
  Clock clock_1 (.out(clock_1_out));
  Adder #(.width(4)) adder_1 (.a(4'b0001), .b(Counter_q), .out(adder_1_out));  // open: cin, cout
  Register #(.width(4)) MAR (.Q(MAR_q));  // open: D, en, clk, clr
  ROM #(.dataWidth(4)) rom_1 (.addr({IR_q, Counter_q}), .data(rom_1_data));
  not not_1 (not_1_out, S1);
  not not_2 (not_2_out, S0);
  Multiplexer #(.select(2), .width(4)) multiplexer_1 (
    .in0(AX_q), .in1(BX_q), .in2(Data), .in3(adder_2_out), .out(multiplexer_1_out), .sel(rom_1_data[3:2]));
  and and_1 (and_1_out, not_2_out, not_1_out);
  and and_2 (and_2_out, S0, not_1_out);
  and and_3 (and_3_out, not_2_out, S1);
  and and_4 (and_4_out, S0, S1);
  Register #(.width(4)) AX (.D(multiplexer_1_out), .en(rom_1_data[0]), .clk(clock_2_out), .Q(AX_q));  // open: clr
  Clock clock_2 (.out(clock_2_out));
  Register #(.width(4)) BX (.D(multiplexer_1_out), .en(rom_1_data[1]), .clk(clock_3_out), .Q(BX_q));  // open: clr
  Clock clock_3 (.out(clock_3_out));
  and and_5 (and_5_out, B0, and_1_out);
  and and_6 (and_6_out, B1, and_2_out);
  and and_7 (and_7_out, B2, and_3_out);
  and and_8 (and_8_out, B3, and_4_out);
  or or_1 (out_8, and_5_out, and_6_out, and_7_out, and_8_out);
  Adder #(.width(4)) adder_2 (.a(AX_q), .b(BX_q), .out(adder_2_out));  // open: cin, cout

  // Notes on the sheet:
  //   contents of rom_1 (hex, n*v repeats v):
  //   5 9 e
endmodule
